# Fritzing sketch Potarray (saved by Fritzing 0.9.3b)

parts:
  U1 = POT [package=pot_mammoth]
  U2 = POT [package=pot_mammoth]
  U3 = POT [package=pot_mammoth]
  U4 = POT [package=pot_mammoth]
  U5 = POT [package=pot_mammoth]
  U6 = POT [package=pot_mammoth]

nets:
  N1: U1.S, U2.S, U3.S, U4.S, U5.S, U6.S
  N2: U1.E, U2.E, U3.E, U4.E, U5.E, U6.E
