# Fritzing sketch TouchInterface (saved by Fritzing 0.9.3b)
breadboards: 1

parts:
  J1 = female pin header, 2 pins [form="♀ (female)"]
  J2 = female pin header, 7 pins [form="♀ (female)"]
  J5 = female pin header, 2 pins [form="♀ (female)"]
  J6 = female pin header, 7 pins [form="♀ (female)"]
  Part1 = Adafruit MPR121
  Part2 = Adafruit MPR121
  J3 = female alternating pin header, 13 pins [form="♀ (female)"]
  J7 = female alternating pin header, 13 pins [form="♀ (female)"]
  J8 = female alternating pin header, 13 pins [form="♀ (female)"]
  J9 = female alternating pin header, 13 pins [form="♀ (female)"]

nets:
  VIN: J1.pin1, J2.pin1, J5.pin1, J6.pin2, Part1.VIN, Part2.VIN
  GND: J1.pin2, J2.pin3, J5.pin2, J6.pin4, Part1.GND, Part2.GND, J3.pin1, J7.pin1, J8.pin1, J9.pin1
  N1: J2.pin2, Part2.3.3V
  N2: J2.pin4, Part2.ADDR
  N3: J2.pin5, J6.pin6, Part1.SDA, Part2.SDA
  N4: J2.pin6, J6.pin7, Part1.SCL, Part2.SCL
  N5: J2.pin7, Part2.IRQ
  N6: J6.pin3, J6.pin5, Part1.3.3V, Part1.ADDR
  N7: Part1.ELEC11, J8.pin13, J9.pin13
  N8: Part1.ELEC10, J8.pin12, J9.pin12
  N9: Part1.ELEC9, J8.pin11, J9.pin11
  N10: Part1.ELEC8, J8.pin10, J9.pin10
  N11: Part1.ELEC7, J8.pin9, J9.pin9
  N12: Part1.ELEC6, J8.pin8, J9.pin8
  N13: Part1.ELEC5, J8.pin7, J9.pin7
  N14: Part1.ELEC4, J8.pin6, J9.pin6
  N15: Part1.ELEC3, J8.pin5, J9.pin5
  N16: Part1.ELEC2, J8.pin4, J9.pin4
  N17: Part1.ELEC1, J8.pin3, J9.pin3
  N18: Part1.ELEC0, J8.pin2, J9.pin2
  N19: Part2.ELEC11, J3.pin13, J7.pin13
  N20: Part2.ELEC10, J3.pin12, J7.pin12
  N21: Part2.ELEC9, J3.pin11, J7.pin11
  N22: Part2.ELEC8, J3.pin10, J7.pin10
  N23: Part2.ELEC7, J3.pin9, J7.pin9
  N24: Part2.ELEC6, J3.pin8, J7.pin8
  N25: Part2.ELEC5, J3.pin7, J7.pin7
  N26: Part2.ELEC4, J3.pin6, J7.pin6
  N27: Part2.ELEC3, J3.pin5, J7.pin5
  N28: Part2.ELEC2, J3.pin4, J7.pin4
  N29: Part2.ELEC1, J3.pin3, J7.pin3
  N30: Part2.ELEC0, J3.pin2, J7.pin2

custom parts:
  Adafruit MPR121: Add lots of touch sensors to your next microcontroller project with this easy-to-use 12-channel capacitive touch sensor breakout board, starring the MPR121. This chip can handle up to 12 individual touch pads. The MPR121 has support for only I2C, which can be implemented with nearly any microcontroller. You can select one of 4 addresses with the ADDR pin, for a total of 48 capacitive touch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
